// Logisim project CSC_270_Final_Project.circ as structural Verilog
module _4_bit_ALU (
  input  [3:0] A,
  input  [3:0] B,
  input  [1:0] ALU_Op,
  output [3:0] ALU_Out
);

  wire and_1_out;
  wire [3:0] adder_1_out, and_2_out, multiplexer_1_out, not_1_out, or_1_out;

  Multiplexer #(.width(4), .enable("false")) multiplexer_1 (
    .in0(B), .in1(not_1_out), .out(multiplexer_1_out), .sel(and_1_out));
  assign not_1_out = ~B;  // NOT_Gate not_1, 4 bits wide
  and and_1 (and_1_out, ALU_Op[0], ALU_Op[1]);
  Adder #(.width(4)) adder_1 (.a(A), .b(multiplexer_1_out), .out(adder_1_out), .cin(and_1_out));  // open: cout
  assign and_2_out = multiplexer_1_out & A;  // AND_Gate and_2, 4 bits wide
  assign or_1_out = multiplexer_1_out | A;  // OR_Gate or_1, 4 bits wide
  Multiplexer #(.select(2), .width(4), .enable("false")) multiplexer_2 (
    .in0(adder_1_out), .in1(and_2_out), .in2(or_1_out), .in3(adder_1_out), .out(ALU_Out), .sel(ALU_Op));

  // Notes on the sheet:
  //   4 Bit ALU
  //   00 = ADD
  //   01 = AND
  //   10 = OR
  //   11 = SUB
  //   sub not B
  //   sub cin
  //   sub
endmodule

module _8x4_bit_Register_File (
  input  [3:0] Data_In,
  input  [2:0] Read_Addr_1,
  input  Write_Enable,
  input  [2:0] Write_Addr,
  input  [2:0] Read_Addr_2,
  input  Clock,
  output [3:0] Read_1_Data,
  output [3:0] Read_2_Data
);

  wire demultiplexer_1_out0, demultiplexer_1_out1, demultiplexer_1_out2, demultiplexer_1_out3,
       demultiplexer_1_out4, demultiplexer_1_out5, demultiplexer_1_out6, demultiplexer_1_out7;
  wire [3:0] register_1_q, register_2_q, register_3_q, register_4_q, register_5_q, register_6_q,
       register_7_q, register_8_q;

  Demultiplexer #(.select(3), .enable("false")) demultiplexer_1 (
    .out0(demultiplexer_1_out0), .out1(demultiplexer_1_out1), .out2(demultiplexer_1_out2),
    .out3(demultiplexer_1_out3), .out4(demultiplexer_1_out4), .out5(demultiplexer_1_out5),
    .out6(demultiplexer_1_out6), .out7(demultiplexer_1_out7), .in(Write_Enable), .sel(Write_Addr));
  Register #(.width(4)) register_1 (
    .D(Data_In), .en(demultiplexer_1_out0), .Q(register_1_q), .clk(Clock));  // open: clr
  Register #(.width(4)) register_2 (
    .D(Data_In), .en(demultiplexer_1_out1), .Q(register_2_q), .clk(Clock));  // open: clr
  Register #(.width(4)) register_3 (
    .D(Data_In), .en(demultiplexer_1_out2), .Q(register_3_q), .clk(Clock));  // open: clr
  Register #(.width(4)) register_4 (
    .D(Data_In), .en(demultiplexer_1_out3), .Q(register_4_q), .clk(Clock));  // open: clr
  Register #(.width(4)) register_5 (
    .D(Data_In), .en(demultiplexer_1_out4), .Q(register_5_q), .clk(Clock));  // open: clr
  Register #(.width(4)) register_6 (
    .D(Data_In), .en(demultiplexer_1_out5), .Q(register_6_q), .clk(Clock));  // open: clr
  Register #(.width(4)) register_7 (
    .D(Data_In), .en(demultiplexer_1_out6), .Q(register_7_q), .clk(Clock));  // open: clr
  Register #(.width(4)) register_8 (
    .D(Data_In), .en(demultiplexer_1_out7), .Q(register_8_q), .clk(Clock));  // open: clr
  Multiplexer #(.select(3), .width(4), .enable("false")) multiplexer_1 (
    .in0(register_1_q), .in1(register_2_q), .in2(register_3_q), .in3(register_4_q), .in4(register_5_q),
    .in5(register_6_q), .in6(register_7_q), .in7(register_8_q), .out(Read_1_Data), .sel(Read_Addr_1));
  Multiplexer #(.select(3), .width(4), .enable("false")) multiplexer_2 (
    .in0(register_1_q), .in1(register_2_q), .in2(register_3_q), .in3(register_4_q), .in4(register_5_q),
    .in5(register_6_q), .in6(register_7_q), .in7(register_8_q), .out(Read_2_Data), .sel(Read_Addr_2));

  // Notes on the sheet:
  //   8x4-bit Register File
endmodule

module ALU_REG_Instruction (
  input  [13:0] in_1,
  input  clock,
  output [3:0] CPU_Op_Out
);

  wire [3:0] bit_extender_1_out, multiplexer_1_out, n8x4_bit_register_file_1_read_1_data,
       n8x4_bit_register_file_1_read_2_data;

  _8x4_bit_Register_File u_8x4_bit_register_file_1 (
    .Data_In(CPU_Op_Out), .Write_Enable(1'b1), .Clock(clock), .Write_Addr(in_1[8:6]),
    .Read_Addr_1(in_1[5:3]), .Read_Addr_2(in_1[2:0]), .Read_1_Data(n8x4_bit_register_file_1_read_1_data),
    .Read_2_Data(n8x4_bit_register_file_1_read_2_data));
  Multiplexer #(.width(4), .enable("false")) multiplexer_1 (
    .in0(n8x4_bit_register_file_1_read_2_data), .in1(bit_extender_1_out), .out(multiplexer_1_out),
    .sel(in_1[13]));
  assign bit_extender_1_out = {{1{in_1[2]}}, in_1[2:0]};  // Bit_Extender bit_extender_1
  _4_bit_ALU u_4_bit_alu_1 (
    .A(n8x4_bit_register_file_1_read_1_data), .B(multiplexer_1_out), .ALU_Op(in_1[10:9]), .ALU_Out(CPU_Op_Out));

  // Notes on the sheet:
  //   op
  //   src2
  //   src1
  //   immed data
  //   immed select
  //   ALU op
  //   dest
endmodule

module ALU_with_MEM (
  input  [13:0] in_1,
  input  clock
);

  wire Control_Logic_i_r, Control_Logic_lw, Control_Logic_sw, not_1_out;
  wire [1:0] Control_Logic_op;
  wire [2:0] multiplexer_1_out;
  wire [3:0] bit_extender_1_out, multiplexer_2_out, multiplexer_3_out, n4_bit_alu_1_alu_out,
       n8x4_bit_register_file_1_read_1_data, n8x4_bit_register_file_1_read_2_data, ram_1_data;

  not not_1 (not_1_out, Control_Logic_sw);
  Control_Logic Control_Logic (
    .IW_first_5(in_1[13:9]), .I_R(Control_Logic_i_r), .SW(Control_Logic_sw), .LW(Control_Logic_lw),
    .OP(Control_Logic_op));
  Multiplexer #(.width(3), .enable("false")) multiplexer_1 (
    .in0(in_1[8:6]), .in1(in_1[2:0]), .out(multiplexer_1_out), .sel(Control_Logic_sw));
  _8x4_bit_Register_File u_8x4_bit_register_file_1 (
    .Data_In(multiplexer_2_out), .Write_Enable(not_1_out), .Clock(clock), .Write_Addr(in_1[8:6]),
    .Read_Addr_1(in_1[5:3]), .Read_Addr_2(multiplexer_1_out),
    .Read_1_Data(n8x4_bit_register_file_1_read_1_data), .Read_2_Data(n8x4_bit_register_file_1_read_2_data));
  assign bit_extender_1_out = {{1{in_1[2]}}, in_1[2:0]};  // Bit_Extender bit_extender_1
  Multiplexer #(.width(4), .enable("false")) multiplexer_2 (
    .in0(n4_bit_alu_1_alu_out), .in1(ram_1_data), .out(multiplexer_2_out), .sel(Control_Logic_lw));
  _4_bit_ALU u_4_bit_alu_1 (
    .A(n8x4_bit_register_file_1_read_1_data), .B(multiplexer_3_out), .ALU_Op(Control_Logic_op),
    .ALU_Out(n4_bit_alu_1_alu_out));
  Multiplexer #(.width(4), .enable("false")) multiplexer_3 (
    .in0(n8x4_bit_register_file_1_read_2_data), .in1(bit_extender_1_out), .out(multiplexer_3_out),
    .sel(Control_Logic_i_r));
  RAM #(.addrWidth(4), .dataWidth(4), .bus("separate")) ram_1 (
    .addr(n4_bit_alu_1_alu_out), .din(n8x4_bit_register_file_1_read_2_data), .data(ram_1_data), .clk(clock));  // open: str, sel, ld, clr

  // Notes on the sheet:
  //   op
  //   src2
  //   WE
  //   src1
  //   immed data
  //   immed select
  //   ALU op
  //   dest
  //   SW
  //   LW
endmodule

module Control_Logic (
  input  [4:0] IW_first_5,
  output I_R,
  output SW,
  output LW,
  output [1:0] OP
);


  assign I_R = IW_first_5[4];
  assign LW = IW_first_5[2];
  assign OP = IW_first_5[1:0];
  assign SW = IW_first_5[3];
endmodule

module Full_CPU__8_bit (
  input  clock
);

  wire Control_Logic_i_r, Control_Logic_lw, Control_Logic_sw, not_1_out;
  wire [1:0] Control_Logic_op;
  wire [2:0] multiplexer_1_out;
  wire [3:0] adder_1_out, ALU_alu_out, bit_extender_1_out, multiplexer_2_out, multiplexer_3_out, PC_q,
       ram_2_data, Reg_read_1_data, Reg_read_2_data;
  wire [13:0] ram_1_data;

  Register #(.width(4)) PC (.D(adder_1_out), .en(1'b1), .Q(PC_q), .clk(clock));  // open: clr
  Adder #(.width(4)) adder_1 (.a(4'b0001), .b(PC_q), .out(adder_1_out));  // open: cin, cout
  RAM #(.addrWidth(4), .dataWidth(14)) ram_1 (.addr(PC_q), .data(ram_1_data), .clk(clock));  // open: sel, ld, clr
  not not_1 (not_1_out, Control_Logic_sw);
  Control_Logic Control_Logic (
    .IW_first_5(ram_1_data[13:9]), .I_R(Control_Logic_i_r), .SW(Control_Logic_sw), .LW(Control_Logic_lw),
    .OP(Control_Logic_op));
  Multiplexer #(.width(3), .enable("false")) multiplexer_1 (
    .in0(ram_1_data[2:0]), .in1(ram_1_data[8:6]), .out(multiplexer_1_out), .sel(Control_Logic_sw));
  _8x4_bit_Register_File Reg (
    .Data_In(multiplexer_2_out), .Write_Enable(not_1_out), .Clock(clock), .Write_Addr(ram_1_data[8:6]),
    .Read_Addr_1(ram_1_data[5:3]), .Read_Addr_2(multiplexer_1_out), .Read_1_Data(Reg_read_1_data),
    .Read_2_Data(Reg_read_2_data));
  assign bit_extender_1_out = {{1{ram_1_data[2]}}, ram_1_data[2:0]};  // Bit_Extender bit_extender_1
  Multiplexer #(.width(4), .enable("false")) multiplexer_2 (
    .in0(ALU_alu_out), .in1(ram_2_data), .out(multiplexer_2_out), .sel(Control_Logic_lw));
  _4_bit_ALU ALU (.A(Reg_read_1_data), .B(multiplexer_3_out), .ALU_Op(Control_Logic_op), .ALU_Out(ALU_alu_out));
  Multiplexer #(.width(4), .enable("false")) multiplexer_3 (
    .in0(Reg_read_2_data), .in1(bit_extender_1_out), .out(multiplexer_3_out), .sel(Control_Logic_i_r));
  RAM #(.addrWidth(4), .dataWidth(4), .bus("separate")) ram_2 (
    .addr(ALU_alu_out), .din(Reg_read_2_data), .data(ram_2_data), .str(Control_Logic_sw), .clk(clock));  // open: sel, ld, clr

  // Notes on the sheet:
  //   Instruction Memory
  //   op
  //   src2
  //   WE
  //   src1
  //   immed data
  //   immed select
  //   ALU op
  //   dest
  //   SW
  //   LW
  //   Data Memory
endmodule

module Full_CPU__16_bit (
  input  clock
);

  wire Control_Logic_i_r, Control_Logic_lw, Control_Logic_sw, not_1_out;
  wire [1:0] Control_Logic_op;
  wire [2:0] multiplexer_1_out;
  wire [15:0] _16_bit_ALU_alu_out, _16_bit_Reg_read_1_data, _16_bit_Reg_read_2_data, adder_1_out,
       multiplexer_2_out, multiplexer_3_out, PC_q, ram_2_data;
  wire [26:0] ram_1_data;

  Register #(.width(16)) PC (.D(adder_1_out), .en(1'b1), .Q(PC_q), .clk(clock));  // open: clr
  Adder #(.width(16)) adder_1 (.a(16'h1), .b(PC_q), .out(adder_1_out));  // open: cin, cout
  RAM #(.addrWidth(16), .dataWidth(27)) ram_1 (.addr(PC_q), .data(ram_1_data), .clk(clock));  // open: sel, ld, clr
  not not_1 (not_1_out, Control_Logic_sw);
  Control_Logic Control_Logic (
    .IW_first_5(ram_1_data[26:22]), .I_R(Control_Logic_i_r), .SW(Control_Logic_sw), .LW(Control_Logic_lw),
    .OP(Control_Logic_op));
  Multiplexer #(.width(3), .enable("false")) multiplexer_1 (
    .in0(ram_1_data[15:13]), .in1(ram_1_data[21:19]), .out(multiplexer_1_out), .sel(Control_Logic_sw));
  _8x16_bit_Register_File _16_bit_Reg (
    .Data_In(multiplexer_2_out), .Write_Enable(not_1_out), .Clock(clock), .Write_Addr(ram_1_data[21:19]),
    .Read_Addr_1(ram_1_data[18:16]), .Read_Addr_2(multiplexer_1_out), .Read_1_Data(_16_bit_Reg_read_1_data),
    .Read_2_Data(_16_bit_Reg_read_2_data));
  Multiplexer #(.width(16), .enable("false")) multiplexer_2 (
    .in0(_16_bit_ALU_alu_out), .in1(ram_2_data), .out(multiplexer_2_out), .sel(Control_Logic_lw));
  _16_bit_ALU _16_bit_ALU (
    .A(_16_bit_Reg_read_1_data), .B(multiplexer_3_out), .ALU_Op(Control_Logic_op),
    .ALU_Out(_16_bit_ALU_alu_out));  // open: Zero
  Multiplexer #(.width(16), .enable("false")) multiplexer_3 (
    .in0(_16_bit_Reg_read_2_data), .in1(ram_1_data[15:0]), .out(multiplexer_3_out), .sel(Control_Logic_i_r));
  RAM #(.addrWidth(16), .dataWidth(16), .bus("separate")) ram_2 (
    .addr(_16_bit_ALU_alu_out), .din(_16_bit_Reg_read_2_data), .data(ram_2_data), .str(Control_Logic_sw),
    .clk(clock));  // open: sel, ld, clr

  // Notes on the sheet:
  //   Instruction Memory
  //   src2
  //   op
  //   WE
  //   imm data
  //   src1
  //   imm select
  //   dest
  //   ALU op
  //   SW
  //   LW
  //   Data Memory
endmodule

module _16_bit_ALU (
  input  [15:0] A,
  input  [15:0] B,
  input  [1:0] ALU_Op,
  output Zero,
  output [15:0] ALU_Out
);

  wire and_1_out;
  wire [15:0] adder_1_out, and_2_out, multiplexer_1_out, not_1_out, or_1_out;

  Multiplexer #(.width(16), .enable("false")) multiplexer_1 (
    .in0(B), .in1(not_1_out), .out(multiplexer_1_out), .sel(and_1_out));
  assign not_1_out = ~B;  // NOT_Gate not_1, 16 bits wide
  and and_1 (and_1_out, ALU_Op[0], ALU_Op[1]);
  Adder #(.width(16)) adder_1 (.a(A), .b(multiplexer_1_out), .out(adder_1_out), .cin(and_1_out));  // open: cout
  assign and_2_out = multiplexer_1_out & A;  // AND_Gate and_2, 16 bits wide
  assign or_1_out = multiplexer_1_out | A;  // OR_Gate or_1, 16 bits wide
  Multiplexer #(.select(2), .width(16), .enable("false")) multiplexer_2 (
    .in0(adder_1_out), .in1(and_2_out), .in2(or_1_out), .in3(adder_1_out), .out(ALU_Out), .sel(ALU_Op));
  Comparator #(.width(16)) comparator_1 (.a({16{1'b0}}), .b(ALU_Out), .eq(Zero));  // open: gt, lt

  // Notes on the sheet:
  //   16 Bit ALU
  //   00 = ADD
  //   01 = AND
  //   10 = OR
  //   11 = SUB
  //   sub not B
  //   sub cin
  //   sub
endmodule

module _8x16_bit_Register_File (
  input  [15:0] Data_In,
  input  [2:0] Read_Addr_1,
  input  Write_Enable,
  input  [2:0] Write_Addr,
  input  [2:0] Read_Addr_2,
  input  Clock,
  output [15:0] Read_1_Data,
  output [15:0] Read_2_Data
);

  wire demultiplexer_1_out0, demultiplexer_1_out1, demultiplexer_1_out2, demultiplexer_1_out3,
       demultiplexer_1_out4, demultiplexer_1_out5, demultiplexer_1_out6, demultiplexer_1_out7;
  wire [15:0] register_1_q, register_2_q, register_3_q, register_4_q, register_5_q, register_6_q,
       register_7_q, register_8_q;

  Demultiplexer #(.select(3), .enable("false")) demultiplexer_1 (
    .out0(demultiplexer_1_out0), .out1(demultiplexer_1_out1), .out2(demultiplexer_1_out2),
    .out3(demultiplexer_1_out3), .out4(demultiplexer_1_out4), .out5(demultiplexer_1_out5),
    .out6(demultiplexer_1_out6), .out7(demultiplexer_1_out7), .in(Write_Enable), .sel(Write_Addr));
  Register #(.width(16)) register_1 (
    .D(Data_In), .en(demultiplexer_1_out0), .Q(register_1_q), .clk(Clock));  // open: clr
  Register #(.width(16)) register_2 (
    .D(Data_In), .en(demultiplexer_1_out1), .Q(register_2_q), .clk(Clock));  // open: clr
  Register #(.width(16)) register_3 (
    .D(Data_In), .en(demultiplexer_1_out2), .Q(register_3_q), .clk(Clock));  // open: clr
  Register #(.width(16)) register_4 (
    .D(Data_In), .en(demultiplexer_1_out3), .Q(register_4_q), .clk(Clock));  // open: clr
  Register #(.width(16)) register_5 (
    .D(Data_In), .en(demultiplexer_1_out4), .Q(register_5_q), .clk(Clock));  // open: clr
  Register #(.width(16)) register_6 (
    .D(Data_In), .en(demultiplexer_1_out5), .Q(register_6_q), .clk(Clock));  // open: clr
  Register #(.width(16)) register_7 (
    .D(Data_In), .en(demultiplexer_1_out6), .Q(register_7_q), .clk(Clock));  // open: clr
  Register #(.width(16)) register_8 (
    .D(Data_In), .en(demultiplexer_1_out7), .Q(register_8_q), .clk(Clock));  // open: clr
  Multiplexer #(.select(3), .width(16), .enable("false")) multiplexer_1 (
    .in0(register_1_q), .in1(register_2_q), .in2(register_3_q), .in3(register_4_q), .in4(register_5_q),
    .in5(register_6_q), .in6(register_7_q), .in7(register_8_q), .out(Read_1_Data), .sel(Read_Addr_1));
  Multiplexer #(.select(3), .width(16), .enable("false")) multiplexer_2 (
    .in0(register_1_q), .in1(register_2_q), .in2(register_3_q), .in3(register_4_q), .in4(register_5_q),
    .in5(register_6_q), .in6(register_7_q), .in7(register_8_q), .out(Read_2_Data), .sel(Read_Addr_2));

  // Notes on the sheet:
  //   8x16-bit Register File
endmodule

module _16_bit_CPU_w__branch (
  input  clock
);

  wire and_1_out, Control_Logic_alusrc, Control_Logic_branch, Control_Logic_memread, Control_Logic_memtoreg,
       Control_Logic_memwrite, Control_Logic_regdest, Control_Logic_regwrite, full_alu_1_zero;
  wire [1:0] Control_Logic_aluop;
  wire [2:0] ALUControl_operation, multiplexer_1_out;
  wire [14:0] ram_1_data;
  wire [15:0] _16_bit_Reg_read_1_data, _16_bit_Reg_read_2_data, adder_1_out, adder_2_out, bit_extender_1_out,
       full_alu_1_alu_out, multiplexer_2_out, multiplexer_3_out, multiplexer_4_out, PC_q, ram_2_data;

  Register #(.width(16)) PC (.D(multiplexer_3_out), .Q(PC_q), .clk(clock));  // open: en, clr
  Adder #(.width(16)) adder_1 (.a(16'h4), .b(PC_q), .out(adder_1_out));  // open: cin, cout
  RAM #(.addrWidth(16), .dataWidth(15)) ram_1 (.addr(PC_q), .data(ram_1_data), .clk(clock));  // open: sel, ld, clr
  Control_Logic__6_bit Control_Logic (
    .in_1(ram_1_data[14:9]), .RegDest(Control_Logic_regdest), .ALUSrc(Control_Logic_alusrc),
    .MemToReg(Control_Logic_memtoreg), .RegWrite(Control_Logic_regwrite), .MemRead(Control_Logic_memread),
    .MemWrite(Control_Logic_memwrite), .Branch(Control_Logic_branch), .ALUOP(Control_Logic_aluop));
  Multiplexer #(.width(3), .enable("false")) multiplexer_1 (
    .in0(ram_1_data[2:0]), .in1(ram_1_data[8:6]), .out(multiplexer_1_out), .sel(Control_Logic_regdest));
  _8x16_bit_Register_File _16_bit_Reg (
    .Data_In(multiplexer_4_out), .Write_Enable(Control_Logic_regwrite), .Clock(clock),
    .Write_Addr(multiplexer_1_out), .Read_Addr_1(ram_1_data[5:3]), .Read_Addr_2(ram_1_data[2:0]),
    .Read_1_Data(_16_bit_Reg_read_1_data), .Read_2_Data(_16_bit_Reg_read_2_data));
  assign bit_extender_1_out = {{13{1'b0}}, ram_1_data[2:0]};  // Bit_Extender bit_extender_1
  Adder #(.width(16)) adder_2 (.a(adder_1_out), .b(bit_extender_1_out), .out(adder_2_out));  // open: cin, cout
  Multiplexer #(.width(16), .enable("false")) multiplexer_2 (
    .in0(_16_bit_Reg_read_2_data), .in1(bit_extender_1_out), .out(multiplexer_2_out),
    .sel(Control_Logic_alusrc));
  ALU_Control ALUControl (.in_1(ram_1_data[14:9]), .in_2(Control_Logic_aluop), .Operation(ALUControl_operation));
  Multiplexer #(.width(16), .enable("false")) multiplexer_3 (
    .in0(adder_1_out), .in1(adder_2_out), .out(multiplexer_3_out), .sel(and_1_out));
  and and_1 (and_1_out, full_alu_1_zero, Control_Logic_branch);
  Full_ALU full_alu_1 (
    .A(_16_bit_Reg_read_1_data), .B(multiplexer_2_out), .ALU_Op(ALUControl_operation),
    .Zero(full_alu_1_zero), .ALU_Out(full_alu_1_alu_out));
  Multiplexer #(.width(16), .enable("false")) multiplexer_4 (
    .in0(full_alu_1_alu_out), .in1(ram_2_data), .out(multiplexer_4_out), .sel(Control_Logic_memtoreg));
  RAM #(.addrWidth(16), .dataWidth(16), .bus("separate")) ram_2 (
    .addr(full_alu_1_alu_out), .din(_16_bit_Reg_read_2_data), .data(ram_2_data),
    .str(Control_Logic_memwrite), .clk(clock), .ld(Control_Logic_memread));  // open: sel, clr

  // Notes on the sheet:
  //   Instruction Memory
  //   op
  //   src2
  //   WE
  //   dest
  //   src1
  //   immed data
  //   RegDest
  //   ALUOP
  //   ALUSrc
  //   Branch
  //   MemToReg
  //   MemWrite
  //   MemRead
  //   Data Memory
endmodule

module Jump (
  input  [15:0] PC,
  input  [15:0] Instruction,
  output [15:0] out_3
);


  assign out_3 = {PC[15:13], Instruction[12:0]};
endmodule

module Control_Logic__6_bit (
  input  [5:0] in_1,
  output RegDest,
  output ALUSrc,
  output MemToReg,
  output RegWrite,
  output MemRead,
  output MemWrite,
  output Branch,
  output [1:0] ALUOP
);

  and and_1 (ALUOP[1], ~in_1[5], ~in_1[4], ~in_1[3], ~in_1[2], ~in_1[1], ~in_1[0]);  // AND_Gate
  and and_2 (MemRead, in_1[5], ~in_1[4], ~in_1[3], ~in_1[2], in_1[1], in_1[0]);  // AND_Gate
  and and_3 (MemWrite, in_1[5], ~in_1[4], in_1[3], ~in_1[2], in_1[1], in_1[0]);  // AND_Gate
  and and_4 (ALUOP[0], ~in_1[5], ~in_1[4], ~in_1[3], in_1[2], ~in_1[1], ~in_1[0]);  // AND_Gate
  or or_1 (ALUSrc, MemRead, MemWrite);
  or or_2 (RegWrite, ALUOP[1], MemRead);

  assign Branch = ALUOP[0];
  assign MemToReg = MemRead;
  assign RegDest = ALUOP[1];

  // Notes on the sheet:
  //   R-format
  //   lw
  //   sw
  //   beq
endmodule

module Full_ALU (
  input  [15:0] A,
  input  [15:0] B,
  input  [2:0] ALU_Op,
  output Zero,
  output [15:0] ALU_Out
);

  wire and_1_out, or_2_out;
  wire [15:0] adder_1_out, and_2_out, multiplexer_1_out, not_1_out, or_1_out;

  Multiplexer #(.width(16), .enable("false")) multiplexer_1 (
    .in0(B), .in1(not_1_out), .out(multiplexer_1_out), .sel(and_1_out));
  assign not_1_out = ~B;  // NOT_Gate not_1, 16 bits wide
  and and_1 (and_1_out, ALU_Op[1], ALU_Op[2]);
  assign and_2_out = A & multiplexer_1_out;  // AND_Gate and_2, 16 bits wide
  assign or_1_out = A | multiplexer_1_out;  // OR_Gate or_1, 16 bits wide
  Adder #(.width(16)) adder_1 (.a(A), .b(multiplexer_1_out), .out(adder_1_out), .cin(and_1_out));  // open: cout
  Multiplexer #(.select(3), .width(16), .enable("false")) multiplexer_2 (
    .in0(and_2_out), .in1(or_1_out), .in2(adder_1_out), .in6(adder_1_out), .out(ALU_Out), .sel(ALU_Op));  // open: in3, in4, in5, in7
  not not_2 (Zero, or_2_out);
  or or_2 (or_2_out, ALU_Out[0], ALU_Out[1], ALU_Out[2], ALU_Out[3], ALU_Out[4], ALU_Out[5], ALU_Out[6], ALU_Out[7], ALU_Out[8], ALU_Out[9], ALU_Out[10], ALU_Out[11], ALU_Out[12], ALU_Out[13], ALU_Out[14], ALU_Out[15]);

  // Notes on the sheet:
  //   000 - AND
  //   001 - OR
  //   010 - ADD
  //   110 - SUB
  //   sub not B
  //   sub cin
  //   sub
endmodule

module ALU_Control (
  input  [5:0] in_1,
  input  [1:0] in_2,
  output [2:0] Operation
);

  wire and_1_out, not_1_out, not_2_out, or_1_out;

  or or_1 (or_1_out, in_1[3], in_1[0]);
  and and_1 (and_1_out, in_2[1], in_1[1]);
  and and_2 (Operation[0], in_2[1], or_1_out);
  or or_2 (Operation[2], in_2[0], and_1_out);
  not not_1 (not_1_out, in_2[1]);
  or or_3 (Operation[1], not_1_out, not_2_out);
  not not_2 (not_2_out, in_1[2]);
endmodule

module _16_bit_CPU_w__b__j (
  input  clock
);

  wire and_1_out, Control_Logic_alusrc, Control_Logic_branch, Control_Logic_memread, Control_Logic_memtoreg,
       Control_Logic_memwrite, Control_Logic_regdest, Control_Logic_regwrite, full_alu_1_zero;
  wire [1:0] Control_Logic_aluop;
  wire [2:0] ALUControl_operation, multiplexer_1_out;
  wire [14:0] ram_1_data;
  wire [15:0] _16_bit_Reg_read_1_data, _16_bit_Reg_read_2_data, adder_1_out, adder_2_out, bit_extender_1_out,
       full_alu_1_alu_out, multiplexer_2_out, multiplexer_3_out, multiplexer_4_out, PC_q, ram_2_data;

  Register #(.width(16)) PC (.D(multiplexer_3_out), .Q(PC_q), .clk(clock));  // open: en, clr
  Adder #(.width(16)) adder_1 (.a(16'h4), .b(PC_q), .out(adder_1_out));  // open: cin, cout
  RAM #(.addrWidth(16), .dataWidth(15)) ram_1 (.addr(PC_q), .data(ram_1_data), .clk(clock));  // open: sel, ld, clr
  Control_Logic__6_bit Control_Logic (
    .in_1(ram_1_data[14:9]), .RegDest(Control_Logic_regdest), .ALUSrc(Control_Logic_alusrc),
    .MemToReg(Control_Logic_memtoreg), .RegWrite(Control_Logic_regwrite), .MemRead(Control_Logic_memread),
    .MemWrite(Control_Logic_memwrite), .Branch(Control_Logic_branch), .ALUOP(Control_Logic_aluop));
  Multiplexer #(.width(3), .enable("false")) multiplexer_1 (
    .in0(ram_1_data[2:0]), .in1(ram_1_data[8:6]), .out(multiplexer_1_out), .sel(Control_Logic_regdest));
  _8x16_bit_Register_File _16_bit_Reg (
    .Data_In(multiplexer_4_out), .Write_Enable(Control_Logic_regwrite), .Clock(clock),
    .Write_Addr(multiplexer_1_out), .Read_Addr_1(ram_1_data[5:3]), .Read_Addr_2(ram_1_data[2:0]),
    .Read_1_Data(_16_bit_Reg_read_1_data), .Read_2_Data(_16_bit_Reg_read_2_data));
  assign bit_extender_1_out = {{13{1'b0}}, ram_1_data[2:0]};  // Bit_Extender bit_extender_1
  Adder #(.width(16)) adder_2 (.a(adder_1_out), .b(bit_extender_1_out), .out(adder_2_out));  // open: cin, cout
  Multiplexer #(.width(16), .enable("false")) multiplexer_2 (
    .in0(_16_bit_Reg_read_2_data), .in1(bit_extender_1_out), .out(multiplexer_2_out),
    .sel(Control_Logic_alusrc));
  ALU_Control ALUControl (.in_1(ram_1_data[14:9]), .in_2(Control_Logic_aluop), .Operation(ALUControl_operation));
  Multiplexer #(.width(16), .enable("false")) multiplexer_3 (
    .in0(adder_1_out), .in1(adder_2_out), .out(multiplexer_3_out), .sel(and_1_out));
  and and_1 (and_1_out, full_alu_1_zero, Control_Logic_branch);
  Full_ALU full_alu_1 (
    .A(_16_bit_Reg_read_1_data), .B(multiplexer_2_out), .ALU_Op(ALUControl_operation),
    .Zero(full_alu_1_zero), .ALU_Out(full_alu_1_alu_out));
  Multiplexer #(.width(16), .enable("false")) multiplexer_4 (
    .in0(full_alu_1_alu_out), .in1(ram_2_data), .out(multiplexer_4_out), .sel(Control_Logic_memtoreg));
  RAM #(.addrWidth(16), .dataWidth(16), .bus("separate")) ram_2 (
    .addr(full_alu_1_alu_out), .din(_16_bit_Reg_read_2_data), .data(ram_2_data),
    .str(Control_Logic_memwrite), .clk(clock), .ld(Control_Logic_memread));  // open: sel, clr

  // Notes on the sheet:
  //   Instruction Memory
  //   op
  //   src2
  //   WE
  //   dest
  //   src1
  //   immed data
  //   RegDest
  //   ALUOP
  //   ALUSrc
  //   Branch
  //   MemToReg
  //   MemWrite
  //   MemRead
  //   Data Memory
endmodule
